# Fritzing sketch Circuit Diagram of Automatic Recharge Keypad Energy Meter (saved by Fritzing 0.8.7b)
breadboards: 1

parts:
  Part1 = Arduino Uno (Rev3)
  M1 = Stepper Motor - Bipolar  # not connected
  Part2 = HC-05 [part_number=HC-05 package="breakout board"]
  L298N1 = L298N DC motor driver
  M2 = Stepper Motor - Bipolar  # not connected
  L298N2 = L298N DC motor driver
  J1 = Basic Servo
  BAT1 = BC9VPC [package=bc9vpc]
  VCC1 = Battery

nets:
  N1: Part1.D8, L298N2.IN3
  N2: Part1.D9_PWM, L298N2.IN2
  N3: Part1.D10_PWM/SS, L298N2.IN1
  N4: Part1.D0/RX, Part2.TXD
  N5: Part1.D1/TX, Part2.RXD
  N6: Part1.D2, J1.pulse
  N7: Part1.D3_PWM, L298N1.IN4
  N8: Part1.D4, L298N1.IN3
  N9: Part1.D5_PWM, L298N1.IN2
  N10: Part1.D6_PWM, L298N1.IN1
  N11: Part1.D7, L298N2.IN4
  VCC: Part1.5V, Part2.VCC, J1.vcc, VCC1.+
  GND: Part1.GND, Part2.GND, J1.gnd, VCC1.-
  12V: L298N1.12V, L298N2.GND, BAT1.V-
  GND_2: L298N1.GND, L298N2.12V, BAT1.V+

custom parts:
  HC-05: A commonly available HC-05 Bluetooth breakout board.
  L298N DC motor driver: 2x DC motor driver with 78M05 positive voltage regulator (7..35 V) L298N: max 46 V, 2 A Set 5 V Enable jumper to enable 5 V regultor (needed for the L298N) and +5 V output at screw terminal or supply external +5 V at screw terminal Set ENA and/or ENB to +5 V to enable motor permanently or supply ENA and/or ENB with PWM signal IN1 and IN2 set rotation directory for motor A (OUT1/OUT2) IN2 and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
